// Logisim project chapter5.circ as structural Verilog: 4 circuits, main circuit main
module main (
  input  [15:0] in_1,
  input  in_2,
  input  [15:0] in_3
);

  RAM #(.addrWidth(16), .dataWidth(16)) ram_1 (
    .addr(in_1), .we(in_2), .oe(in_2), .clk(in_2), .din(in_3));  // open: dout
endmodule

module Memory (
  input  [15:0] keyboardIn,
  input  [15:0] i,
  input  load,
  input  [14:0] address,
  output [15:0] screenOut,
  output [15:0] o
);

  wire demultiplexer_1_out0, demultiplexer_1_out1, demultiplexer_1_out2, or_1_out;
  wire [15:0] DataMemory_dout, Keyboard_q;

  Demultiplexer #(.select(2)) demultiplexer_1 (
    .out0(demultiplexer_1_out0), .out1(demultiplexer_1_out1), .out2(demultiplexer_1_out2), .in(load),
    .sel(address[14:13]));  // open: out3
  or or_1 (or_1_out, demultiplexer_1_out0, demultiplexer_1_out1);
  RAM #(.addrWidth(14), .dataWidth(16)) DataMemory (
    .addr(address[13:0]), .we(or_1_out), .oe(or_1_out), .clk(or_1_out), .din(i), .dout(DataMemory_dout));
  RAM #(.addrWidth(13), .dataWidth(16)) Screen (
    .addr(address[12:0]), .we(demultiplexer_1_out2), .oe(demultiplexer_1_out2), .clk(demultiplexer_1_out2),
    .din(i), .dout(screenOut));
  Register #(.trigger("high"), .width(16)) Keyboard (.D(keyboardIn), .clk(1'b1), .Q(Keyboard_q));  // open: en, clr
  Multiplexer #(.select(2), .width(16)) multiplexer_1 (
    .in0(DataMemory_dout), .in1(DataMemory_dout), .in2(screenOut), .in3(Keyboard_q), .out(o),
    .sel(address[14:13]));
endmodule

module CPU (
  input  [15:0] instruction,
  input  [15:0] inM,
  input  reset,
  input  clock,
  output [15:0] outM,
  output writeM,
  output [14:0] addressM,
  output [14:0] pc
);

  wire alu_1_ng, alu_1_zr, and_1_out, and_2_out, and_3_out, not_1_out, not_2_out, or_1_out, or_2_out,
       or_3_out;
  wire [14:0] multiplexer_1_out;
  wire [15:0] DRegister_q, multiplexer_2_out, multiplexer_3_out;
  wire [15:15] ARegister_q, pc_optimize_1_o;

  Multiplexer #(.width(15)) multiplexer_1 (
    .in0({15{1'b0}}), .in1(instruction[14:0]),
    .out({multiplexer_1_out[14:4], writeM, multiplexer_1_out[2:0]}), .sel(instruction[15]));
  Multiplexer #(.width(16)) multiplexer_2 (.in0(outM), .in1(instruction), .out(multiplexer_2_out), .sel(not_1_out));
  not not_1 (not_1_out, instruction[15]);
  or or_1 (or_1_out, multiplexer_1_out[5], not_1_out);
  Register #(.width(16)) DRegister (.D(outM), .clk(multiplexer_1_out[4]), .Q(DRegister_q));  // open: en, clr
  Register #(.trigger("high"), .width(16)) ARegister (
    .D(multiplexer_2_out), .clk(or_1_out), .Q({ARegister_q[15], addressM}));  // open: en, clr
  Multiplexer #(.width(16)) multiplexer_3 (
    .in0({ARegister_q[15], addressM}), .in1(inM), .out(multiplexer_3_out), .sel(multiplexer_1_out[12]));
  and and_1 (and_1_out, multiplexer_1_out[0], not_2_out);
  and and_2 (and_2_out, multiplexer_1_out[2], alu_1_ng);
  or or_2 (or_2_out, and_2_out, and_3_out);
  or or_3 (or_3_out, and_1_out, or_2_out);
  and and_3 (and_3_out, multiplexer_1_out[1], alu_1_zr);
  PC_Optimize pc_optimize_1 (
    .i({ARegister_q[15], addressM}), .inc(1'b1), .load(or_3_out), .reset(reset), .clock(clock),
    .o({pc_optimize_1_o[15], pc}));
  ALU alu_1 (
    .x(DRegister_q), .y(multiplexer_3_out), .zx(multiplexer_1_out[11]), .nx(multiplexer_1_out[10]),
    .zy(multiplexer_1_out[9]), .ny(multiplexer_1_out[8]), .f(multiplexer_1_out[7]),
    .no(multiplexer_1_out[6]), .ot(outM), .zr(alu_1_zr), .ng(alu_1_ng));
  not not_2 (not_2_out, alu_1_ng);
endmodule

module Computer (
  input  [15:0] keyboardIn,
  input  reset,
  output [15:0] screenOut,
  output [15:0] cpuOut,
  output [15:0] out_5,
  output [14:0] out_6
);

  wire clock_1_out, cpu_1_writem;
  wire [14:0] cpu_1_addressm;
  wire [15:0] ram_1_dout;

  ROM #(.addrWidth(15), .dataWidth(16)) InstrucitonMemory (.addr(out_6), .data(out_5));
  Clock clock_1 (.out(clock_1_out));
  CPU cpu_1 (
    .instruction(out_5), .inM(ram_1_dout), .reset(reset), .clock(clock_1_out), .outM(cpuOut),
    .writeM(cpu_1_writem), .addressM(cpu_1_addressm), .pc(out_6));
  RAM #(.addrWidth(15), .dataWidth(16)) ram_1 (
    .addr(cpu_1_addressm), .we(cpu_1_writem), .oe(cpu_1_writem), .clk(cpu_1_writem), .din(cpuOut),
    .dout(ram_1_dout));

  // Notes on the sheet:
  //   contents of InstrucitonMemory (hex, n*v repeats v):
  //   2 ea48 0 f810 15 e304 1 f810 15 e304 0 f908 f810 15 e304 1 f810 2 f088 a ea47 15 ea47
endmodule
